# Fritzing sketch Mini_MP3_Player (saved by Fritzing 0.9.9b)

parts:
  Part1 = Arduino Nano (Rev3.0)
  DFPlayer_Mini1 = DFPlayer MINI [package="DIP (Dual Inline) [THT]"]
  Squix1 = OLED 0.96" 128x64 I2C SSD1306
  Matrix_keypad1 = KEYPAD 4x4
  SP1 = SPEAKER [package=pcb_mount_speaker]

nets:
  GND: Part1.GND, DFPlayer_Mini1.GND, Squix1.GND
  N1: Part1.D2, Matrix_keypad1.col1
  N2: Part1.D3, Matrix_keypad1.col2
  N3: Part1.D4, Matrix_keypad1.col3
  N4: Part1.D6, Matrix_keypad1.row1
  N5: Part1.D7, Matrix_keypad1.row2
  N6: Part1.D8, Matrix_keypad1.row3
  N7: Part1.D9, Matrix_keypad1.row4
  N8: Part1.D10, DFPlayer_Mini1.TX
  N9: Part1.D11/MOSI, DFPlayer_Mini1.RX
  5V: Part1.5V, DFPlayer_Mini1.VCC
  N10: Part1.A5, Squix1.SCL
  N11: Part1.A4, Squix1.SCA
  3V3: Part1.3V3, Squix1.VCC
  N12: DFPlayer_Mini1.SPK1, SP1.-
  N13: DFPlayer_Mini1.SPK2, SP1.+

custom parts:
  DFPlayer MINI: MP3 module by DFRobot.com for playing Music from an SD-Card. Supports WAV and MP3 files.
  KEYPAD 4x4: Matrix keypad 16 buttons, 4 rows x 4 columns
